// Logisim project Add_1.circ as structural Verilog: 2 circuits, main circuit Add_1
module Add_1 (
  input  A,
  input  B,
  input  C,
  output S,
  output VAI_1
);

  wire and_1_out, and_2_out, or_1_out, xor_1_out;

  xor xor_1 (xor_1_out, C, B);
  or or_1 (or_1_out, C, B);
  xor xor_2 (S, xor_1_out, A);
  and and_1 (and_1_out, or_1_out, A);
  and and_2 (and_2_out, C, B);
  or or_2 (VAI_1, and_1_out, and_2_out);
endmodule

module main (
  input  in_1,
  input  in_2,
  input  in_3,
  output out_4,
  output out_5
);

  Add_1 add_1_1 (.S(out_5), .VAI_1(out_4), .A(in_1), .B(in_2), .C(in_3));
endmodule
