// Logisim project Subtradores.circ as structural Verilog
module Sub_1 (
  input  A,
  input  B,
  input  VEM_1,
  output S,
  output VAI_1
);

  wire and_1_out, and_2_out, or_1_out, xor_1_out;

  xor xor_1 (xor_1_out, A, B);
  or or_1 (or_1_out, B, VEM_1);
  xor xor_2 (S, xor_1_out, VEM_1);
  and and_1 (and_1_out, or_1_out, ~VEM_1);  // AND_Gate
  and and_2 (and_2_out, A, B);
  or or_2 (VAI_1, and_1_out, and_2_out);
endmodule

module Sub_4 (
  input  [3:0] B,
  input  [3:0] A,
  output OverFlow,
  output [3:0] S
);

  wire sub_1_2_vai_1, sub_1_3_vai_1, sub_1_4_vai_1;

  // Probe on A
  Sub_1 sub_1_1 (.S(S[3]), .VAI_1(OverFlow), .A(A[3]), .B(B[3]), .VEM_1(sub_1_2_vai_1));
  Sub_1 sub_1_2 (.S(S[2]), .VAI_1(sub_1_2_vai_1), .A(A[2]), .B(B[2]), .VEM_1(sub_1_3_vai_1));
  Sub_1 sub_1_3 (.S(S[1]), .VAI_1(sub_1_3_vai_1), .A(A[1]), .B(B[1]), .VEM_1(sub_1_4_vai_1));
  // Probe on S
  Sub_1 sub_1_4 (.S(S[0]), .VAI_1(sub_1_4_vai_1), .A(A[0]), .B(B[0]), .VEM_1(1'b0));
  // Probe on B
endmodule
